// Logisim project ioPort.circ as structural Verilog
module IOPorts (
  input  in_1,
  input  in_2,
  input  PA0,
  input  in_4,
  input  Read_Data,
  input  in_6,
  input  in_7,
  input  in_8,
  input  in_9,
  output out_10
);

  wire d_ff_1_q, d_ff_2_q, d_ff_3_q, not_1_out, transistor_1_out;

  Transistor #(.gate("br")) transistor_1 (.in(PA0), .out(transistor_1_out), .gate(not_1_out));
  Pull_Resistor #(.pull(1)) pull_resistor_1 (.node(transistor_1_out));
  not not_1 (not_1_out, in_1);
  assign PA0 = d_ff_2_q ? d_ff_3_q : 1'bz;  // Controlled_Buffer controlled_buffer_1
  D_Flip_Flop d_ff_1 (.clk(in_9), .D(PA0), .Q(d_ff_1_q));  // open: Qn, preset, en, reset
  D_Flip_Flop d_ff_2 (.clk(in_4), .D(out_10), .Q(d_ff_2_q), .reset(in_2));  // open: Qn, preset, en
  D_Flip_Flop d_ff_3 (.clk(in_7), .D(out_10), .Q(d_ff_3_q), .reset(in_2));  // open: Qn, preset, en
  assign out_10 = in_8 ? d_ff_1_q : 1'bz;  // Controlled_Buffer controlled_buffer_2
  assign out_10 = Read_Data ? d_ff_2_q : 1'bz;  // Controlled_Buffer controlled_buffer_3
  assign out_10 = in_6 ? d_ff_3_q : 1'bz;  // Controlled_Buffer controlled_buffer_4
  // Probe on out_10

  // Other names for the same wires on the sheet: CLK = in_9; PUD = in_1; RDA0 = Read_Data; RESET = in_2; RPA0 = in_8;
  //   RRA0 = in_6; WDA0 = in_4; WRA0 = in_7

  // Notes on the sheet:
  //   Write Data
  //   Read 
  //   PINA0
  //   DDRA0
  //   PORTA0
endmodule

module PORTA (
  input  in_1,
  input  in_2,
  input  in_3
);

  wire button_1_out, clock_1_out, clock_2_out;
  wire [3:0] counter_1_q;
  wire [7:0] rom_1_data;

  Counter #(.width(4), .max('hf)) counter_1 (
    .Q(counter_1_q), .clk(clock_1_out), .clr(button_1_out));  // open: load, D, count, carry
  Clock clock_1 (.out(clock_1_out));
  Button button_1 (.out(button_1_out));
  // Probe on counter_1_q
  ROM #(.addrWidth(4)) rom_1 (.addr(counter_1_q), .data(rom_1_data));  // open: sel
  Clock clock_2 (.out(clock_2_out));
  IOPorts ioports_1 (
    .in_1(in_1), .in_2(rom_1_data[5]), .PA0(in_2), .in_4(rom_1_data[4]), .Read_Data(rom_1_data[3]),
    .in_6(rom_1_data[2]), .in_7(rom_1_data[1]), .in_9(clock_2_out), .in_8(rom_1_data[0]), .out_10(in_3));
  // Probe on in_3

  // Notes on the sheet:
  //   DDR=0: INPUT
  //   DDR=1: OUTPUT
  //   contents of rom_1 (hex, n*v repeats v):
  //   20 10 1 0 3 0 4 0 5 0 6 0 7 0 8
endmodule

module MPIO (
  input  PUD,
  input  Reset,
  input  WDA0,
  input  RDA0,
  input  RRA0,
  input  WRA0,
  input  RPA0,
  input  CLK,
  input  [7:0] in_9,
  output [7:0] out_10
);

  IOPorts ioports_1 (
    .in_1(PUD), .in_2(Reset), .PA0(in_9[0]), .in_4(WDA0), .Read_Data(RDA0), .in_6(RDA0), .in_7(WRA0),
    .in_9(CLK), .in_8(RPA0), .out_10(out_10[0]));
  IOPorts ioports_2 (
    .in_1(PUD), .in_2(Reset), .PA0(in_9[1]), .in_4(WDA0), .Read_Data(RDA0), .in_6(RDA0), .in_7(WRA0),
    .in_9(CLK), .in_8(RPA0), .out_10(out_10[1]));
  IOPorts ioports_3 (
    .in_1(PUD), .in_2(Reset), .PA0(in_9[2]), .in_4(WDA0), .Read_Data(RDA0), .in_6(RDA0), .in_7(WRA0),
    .in_9(CLK), .in_8(RPA0), .out_10(out_10[2]));
  IOPorts ioports_4 (
    .in_1(PUD), .in_2(Reset), .PA0(in_9[3]), .in_4(WDA0), .Read_Data(RDA0), .in_6(RDA0), .in_7(WRA0),
    .in_9(CLK), .in_8(RPA0), .out_10(out_10[3]));
  IOPorts ioports_5 (
    .in_1(PUD), .in_2(Reset), .PA0(in_9[4]), .in_4(WDA0), .Read_Data(RDA0), .in_6(RDA0), .in_7(WRA0),
    .in_9(CLK), .in_8(RPA0), .out_10(out_10[4]));
  IOPorts ioports_6 (
    .in_1(PUD), .in_2(Reset), .PA0(in_9[5]), .in_4(WDA0), .Read_Data(RDA0), .in_6(RDA0), .in_7(WRA0),
    .in_9(CLK), .in_8(RPA0), .out_10(out_10[5]));
  IOPorts ioports_7 (
    .in_1(PUD), .in_2(Reset), .PA0(in_9[6]), .in_4(WDA0), .Read_Data(RDA0), .in_6(RDA0), .in_7(WRA0),
    .in_9(CLK), .in_8(RPA0), .out_10(out_10[6]));
  IOPorts ioports_8 (
    .in_1(PUD), .in_2(Reset), .PA0(in_9[7]), .in_4(WDA0), .Read_Data(RDA0), .in_6(RDA0), .in_7(WRA0),
    .in_9(CLK), .in_8(RPA0), .out_10(out_10[7]));

  assign RRA0 = RDA0;
endmodule
